// Digital circuit 4bit-counter.dig as structural Verilog
module _4bit_counter (
  input  clk,
  input  CLR,
  output [3:0] COUNT
);

  wire [3:0] _4bit_full_adder_1_sum;

  _4bit_register _4bit_register_1 (.D(_4bit_full_adder_1_sum), .CLK(clk), .CLR(CLR), .Q(COUNT));
  _4bit_full_adder _4bit_full_adder_1 (.A(COUNT), .B(4'b0001), .Cin(1'b0), .SUM(_4bit_full_adder_1_sum));  // open: Cout
  // Probe on _4bit_full_adder_1_sum
endmodule
