// Digital circuit 4bit-full-adder.dig as structural Verilog
module _4bit_full_adder (
  input  [3:0] A,
  input  Cin,
  input  [3:0] B,
  output [3:0] SUM,
  output Cout
);

  wire _1bit_full_adder_1_c_out, _1bit_full_adder_3_c_out, _1bit_full_adder_4_c_out;

  _1bit_full_adder _1bit_full_adder_1 (.A(A[0]), .B(B[0]), .C_in(Cin), .SUM(SUM[0]), .C_out(_1bit_full_adder_1_c_out));
  _1bit_full_adder _1bit_full_adder_2 (.A(A[0]), .B(B[0]), .C_in(Cin), .SUM(SUM[0]), .C_out(_1bit_full_adder_1_c_out));
  _1bit_full_adder _1bit_full_adder_3 (
    .A(A[1]), .B(B[1]), .C_in(_1bit_full_adder_1_c_out), .SUM(SUM[1]), .C_out(_1bit_full_adder_3_c_out));
  _1bit_full_adder _1bit_full_adder_4 (
    .A(A[2]), .B(B[2]), .C_in(_1bit_full_adder_3_c_out), .SUM(SUM[2]), .C_out(_1bit_full_adder_4_c_out));
  _1bit_full_adder _1bit_full_adder_5 (.A(A[3]), .B(B[3]), .C_in(_1bit_full_adder_4_c_out), .SUM(SUM[3]), .C_out(Cout));
endmodule
