// Digital circuit add4_main.dig as structural Verilog
module add4_main (
  input  [3:0] A,
  input  [3:0] B,
  input  Cin,
  output [3:0] SUM,
  output Cout
);

  _4bit_full_adder _4bit_full_adder_1 (.A(A), .B(B), .Cin(Cin), .SUM(SUM), .Cout(Cout));
endmodule
