// Digital circuit d-flipflop.dig as structural Verilog
module d_flipflop (
  input  D,
  input  CLK,
  output Q
);

  wire d_latch_1_q, not_1_out;

  not not_1 (not_1_out, CLK);
  d_latch d_latch_1 (.CLK(not_1_out), .D(D), .Q(d_latch_1_q));  // open: nQ
  d_latch d_latch_2 (.CLK(CLK), .D(d_latch_1_q), .Q(Q));  // open: nQ
endmodule
