// Digital circuit rom-test.dig as structural Verilog
module rom_test (
  input  [7:0] ADDR,
  output [31:0] IW,
  output [23:0] BXCODE
);

  ROM #(.AddrBits(8), .Bits(32)) Instruction_Memory (.A(ADDR), .sel(1'b1), .D({IW[31:28], BXCODE, IW[3:0]}));

  assign IW[27:4] = BXCODE;

  // Notes on the sheet:
  //   contents of Instruction_Memory (hex, n*v repeats v):
  //   e24dd008,e58de000,e3500000,1a000001,e3a00001,ea000004,e58d0004,e2400001,ebfffff6,
  //   e59d1004,e0000091,e59de000,e28dd008,e12fff1e,e2800000
endmodule
