// Digital circuit 4bit-adder.dig as structural Verilog
module _4bit_adder (
  input  [3:0] A,
  input  [3:0] B,
  input  C_in,
  output [3:0] SUM,
  output C_out
);

  wire _1bit_full_adder_1_c_out, _1bit_full_adder_2_c_out, _1bit_full_adder_3_c_out;

  _1bit_full_adder _1bit_full_adder_1 (.A(A[0]), .B(B[0]), .C_in(C_in), .SUM(SUM[0]), .C_out(_1bit_full_adder_1_c_out));
  _1bit_full_adder _1bit_full_adder_2 (
    .A(A[1]), .B(B[1]), .C_in(_1bit_full_adder_1_c_out), .SUM(SUM[1]), .C_out(_1bit_full_adder_2_c_out));
  _1bit_full_adder _1bit_full_adder_3 (
    .A(A[2]), .B(B[2]), .C_in(_1bit_full_adder_2_c_out), .SUM(SUM[2]), .C_out(_1bit_full_adder_3_c_out));
  _1bit_full_adder _1bit_full_adder_4 (
    .A(A[3]), .B(B[3]), .C_in(_1bit_full_adder_3_c_out), .SUM(SUM[3]), .C_out(C_out));
endmodule
