// Digital circuit 4bit-counter.dig as structural Verilog
module _4bit_counter (
  input  clk,
  input  CLR,
  output [3:0] COUNT
);

  wire [3:0] _4bit_adder_1_sum;

  _4bit_register_clr _4bit_register_clr_1 (.D(_4bit_adder_1_sum), .CLK(clk), .CLR(CLR), .Q(COUNT));
  _4bit_adder _4bit_adder_1 (.A(COUNT), .B(4'b0001), .SUM(_4bit_adder_1_sum), .C_in(1'b0));  // open: C_out
endmodule
