// Digital circuit 4bit-register-clr.dig as structural Verilog
module _4bit_register_clr (
  input  [3:0] D,
  input  CLK,
  input  CLR,
  output [3:0] Q
);

  d_flipflop_clr d_flipflop_clr_1 (.D(D[0]), .CLK(CLK), .CLR(CLR), .Q(Q[0]));
  d_flipflop_clr d_flipflop_clr_2 (.D(D[1]), .CLK(CLK), .CLR(CLR), .Q(Q[1]));
  d_flipflop_clr d_flipflop_clr_3 (.D(D[2]), .CLK(CLK), .CLR(CLR), .Q(Q[2]));
  d_flipflop_clr d_flipflop_clr_4 (.D(D[3]), .CLK(CLK), .CLR(CLR), .Q(Q[3]));
endmodule
