// Digital circuit add-main.dig as structural Verilog
module add_main (
  input  [3:0] A,
  input  [3:0] B,
  input  clk,
  output [3:0] SUM,
  output out_5
);

  _4bit_adder _4bit_adder_1 (.A(A), .B(B), .SUM(SUM), .C_in(1'b0));  // open: C_out
endmodule
